# Fritzing sketch 4chFanControllerUNO (saved by Fritzing 0.7.12b)
breadboards: 1

parts:
  Q1 = Basic FET P-Channel [part_number=TIP120 package="TO220 [THT]"]
  Q3 = Basic FET P-Channel [part_number=TIP120 package="TO220 [THT]"]
  Q4 = Basic FET P-Channel [part_number=TIP120 package="TO220 [THT]"]
  1000µF = Electrolytic Capacitor [capacitance=10µF voltage=35V package="300 mil [THT, electrolytic]"]
  1000µF_2 = Electrolytic Capacitor [capacitance=999µF voltage=35V package="300 mil [THT, electrolytic]"]
  1000µF_3 = Electrolytic Capacitor [capacitance=10µF voltage=35V package="300 mil [THT, electrolytic]"]
  Q5 = Basic FET P-Channel [part_number=TIP120 package="TO220 [THT]"]
  1000µF_4 = Electrolytic Capacitor [capacitance=47µF voltage=35V package="300 mil [THT, electrolytic]"]
  2Ω = Resistor [tolerance=±5% resistance=2.2 power=10 package=THT]
  2Ω_2 = Resistor [tolerance=±5% resistance=2.2 power=10 package=THT]
  2Ω_3 = Resistor [tolerance=±5% resistance=2.2 power=10 package=THT]
  2Ω_4 = Resistor [tolerance=±5% resistance=2.2 power=10 package=THT]
  1kΩ = Resistor [tolerance=±5% resistance=1k power=10 package=THT]
  1kΩ_2 = Resistor [tolerance=±5% resistance=1k power=10 package=THT]
  1kΩ_3 = Resistor [tolerance=±5% resistance=1k power=10 package=THT]
  1kΩ_4 = Resistor [tolerance=±5% resistance=1k power=10 package=THT]
  CPU_Fan = DC Motor
  SYS_Fan = DC Motor
  HD_Fan = DC Motor
  GPU_Fan = DC Motor
  D1 = Rectifier Diode [part_number=1N4001 package="300 mil [THT]"]
  D2 = Rectifier Diode [part_number=1N4001 package="300 mil [THT]"]
  D3 = Rectifier Diode [part_number=1N4001 package="300 mil [THT]"]
  D4 = Rectifier Diode [part_number=1N4001 package="300 mil [THT]"]
  Fuse1 = Fuse with Handler [part_number=Htc-15m]
  Arduino_UNO_R3 = Arduino
  TM1803_RGB_LED_Strip = female pin header, 3 pins [form="♀ (female)"]
  Power_plug1 = Power plug

nets (from the schematic view):
  N1: Q1.gate, 1kΩ.Pin_0
  N2: Q1.drain, 2Ω_4.Pin_0
  GND: Q1.source, Q3.source, Q4.source, Q5.source, Arduino_UNO_R3.GND, TM1803_RGB_LED_Strip.pin3, Power_plug1.GND
  N3: Q3.gate, 1kΩ_2.Pin_0
  N4: Q3.drain, 2Ω_3.Pin_0
  N5: Q4.gate, 1kΩ_3.Pin_0
  N6: Q4.drain, 2Ω_2.Pin_0
  N7: 1000µF.-, 2Ω_3.Pin_1, HD_Fan.pin_1, D3.anode
  N8: 1000µF.+, 1000µF_2.+, 1000µF_3.+, 1000µF_4.+, CPU_Fan.pin_2, SYS_Fan.pin_2, HD_Fan.pin_2, GPU_Fan.pin_2, D1.cathode, D2.cathode, D3.cathode, D4.cathode, Fuse1.Connector1, TM1803_RGB_LED_Strip.pin2
  N9: 1000µF_2.-, 2Ω_4.Pin_1, GPU_Fan.pin_1, D4.anode
  N10: 1000µF_3.-, 2Ω_2.Pin_1, SYS_Fan.pin_1, D2.anode
  N11: Q5.gate, 1kΩ_4.Pin_0
  N12: Q5.drain, 2Ω.Pin_0
  N13: 1000µF_4.-, 2Ω.Pin_1, CPU_Fan.pin_1, D1.anode
  N14: 1kΩ.Pin_1, Arduino_UNO_R3.D9
  N15: 1kΩ_2.Pin_1, Arduino_UNO_R3.D6
  N16: 1kΩ_3.Pin_1, Arduino_UNO_R3.D5
  N17: 1kΩ_4.Pin_1, Arduino_UNO_R3.D3
  N18: Fuse1.Connector2, Power_plug1.VCC
  N19: Arduino_UNO_R3.A0, TM1803_RGB_LED_Strip.pin1

notes:
  To TM1803 RGB LED Strip.
  aka. Radio Shack PN#2760249
  0.3
